// Logisim project cpu.circ as structural Verilog: 6 circuits, main circuit main
module main (
  input  in_1
);

  wire button_1_out, button_2_out, cpu_1_external_clock, extern_out_2_clock, or_1_out;
  wire [6:0] keyboard_1_data;
  wire [15:0] cpu_1_rom_addr, extern_out_1_output, extern_out_2_output;
  wire [16:0] cpu_1_external_out;
  wire [23:0] rom_1_data;

  Keyboard #(.trigger("falling")) keyboard_1 (
    .clk(cpu_1_external_clock), .data(keyboard_1_data));  // open: re, clr, avail
  CPU cpu_1 (
    .Enable(in_1), .External_Out(cpu_1_external_out), .ROM_Addr(cpu_1_rom_addr), .ROM_Instr(rom_1_data),
    .External_In({{9{1'b0}}, keyboard_1_data}), .Reset(button_1_out), .External_Clock(cpu_1_external_clock));
  Button button_1 (.out(button_1_out));
  ROM #(.addrWidth(16), .dataWidth(24)) rom_1 (.addr(cpu_1_rom_addr), .data(rom_1_data));  // open: sel
  Hex_Digit_Display hex_digit_display_1 (.value(extern_out_1_output[15:12]));  // open: dp
  extern_out extern_out_1 (.Input(cpu_1_external_out), .Output(extern_out_1_output));  // open: Clock
  extern_out extern_out_2 (.Input(cpu_1_external_out), .Output(extern_out_2_output), .Clock(extern_out_2_clock));
  TTY #(.trigger("falling")) tty_1 (
    .data(extern_out_2_output[6:0]), .clk(extern_out_2_clock), .clr(or_1_out));  // open: we
  Button button_2 (.out(button_2_out));
  Hex_Digit_Display hex_digit_display_2 (.value(extern_out_1_output[11:8]));  // open: dp
  Hex_Digit_Display hex_digit_display_3 (.value(extern_out_1_output[7:4]));  // open: dp
  or or_1 (or_1_out, extern_out_2_output[15], button_2_out);
  Hex_Digit_Display hex_digit_display_4 (.value(extern_out_1_output[3:0]));  // open: dp

  // Notes on the sheet:
  //   Keyboard Input
  //   contents of rom_1 (hex, n*v repeats v):
  //   b00000 300001 700000 300001 400000 d00000 100000 a00000
  //   Hex Output
  //   TTY Output
endmodule

module CPU (
  input  [23:0] ROM_Instr,
  input  [15:0] External_In,
  input  Enable,
  input  Reset,
  output [15:0] ROM_Addr,
  output External_Clock,
  output [16:0] External_Out
);

  wire adder_1_cout, alu_1_flag, and_1_out, and_2_out, clock_1_out, counter_1_q, decoder_1_j,
       decoder_1_jmp_if_flag_or_j, decoder_1_low_jmp_ram__high_jmp_input,
       decoder_1_low_ram_addr_input__high_ram_addr_rreg, decoder_1_write_output, decoder_1_write_ra,
       decoder_1_write_ram, decoder_1_write_rb, decoder_1_write_rreg, not_1_out, not_2_out, or_1_out;
  wire [15:0] adder_1_out, mux_16_1_output, mux_16_2_output, mux_16_3_output, mux_16_4_output,
       mux_16_5_output, RA_q, ram_1_data, RB_q, register_2_q;

  Adder #(.width(16)) adder_1 (.a(ROM_Addr), .b(16'h1), .out(adder_1_out), .cout(adder_1_cout));  // open: cin
  not not_1 (not_1_out, adder_1_cout);
  Clock clock_1 (.out(clock_1_out));
  mux_16 mux_16_1 (.Input_A(adder_1_out), .Input_B(External_Out[15:0]), .Output(mux_16_1_output), .Select(or_1_out));
  and and_1 (and_1_out, not_1_out, Enable, clock_1_out);
  Register #(.width(16), .trigger("falling")) register_1 (
    .D(mux_16_1_output), .Q(ROM_Addr), .clk(and_1_out), .clr(Reset));  // open: en
  decoder decoder_1 (
    .in_1(ROM_Instr[23:20]), .Low_RAM__High_INPUT(External_Clock), .Write_RA(decoder_1_write_ra),
    .Write_RB(decoder_1_write_rb), .Write_RAM(decoder_1_write_ram),
    .Low_JMP_RAM__High_JMP_INPUT(decoder_1_low_jmp_ram__high_jmp_input),
    .JMP_if_FLAG_or_J(decoder_1_jmp_if_flag_or_j), .J(decoder_1_j), .Write_OUTPUT(decoder_1_write_output),
    .Read_INPUT(External_Out[16]), .Write_RREG(decoder_1_write_rreg),
    .Low_RAM_addr_INPUT__High_RAM_addr_RREG(decoder_1_low_ram_addr_input__high_ram_addr_rreg));  // open: Enable
  mux_16 mux_16_2 (
    .Input_A(mux_16_4_output), .Input_B(ram_1_data), .Output(mux_16_2_output), .Select(decoder_1_write_ram));
  mux_16 mux_16_3 (
    .Input_A(mux_16_4_output), .Input_B(ram_1_data), .Output(mux_16_3_output), .Select(decoder_1_write_ram));
  not not_2 (not_2_out, decoder_1_write_ra);
  mux_16 mux_16_4 (.Input_A(External_In), .Input_B(ROM_Instr[15:0]), .Output(mux_16_4_output), .Select(not_2_out));
  Register #(.width(16), .trigger("falling")) RA (
    .D(mux_16_2_output), .Q(RA_q), .clk(decoder_1_write_rb));  // open: en, clr
  Register #(.width(16), .trigger("falling")) RB (
    .D(mux_16_3_output), .Q(RB_q), .clk(decoder_1_low_jmp_ram__high_jmp_input));  // open: en, clr
  mux_16 mux_16_5 (
    .Input_A(mux_16_4_output), .Input_B(ram_1_data), .Output(mux_16_5_output), .Select(decoder_1_write_ram));
  alu alu_1 (
    .Input_A(RA_q), .Input_B(RB_q), .Output(External_Out[15:0]), .Operation(ROM_Instr[19:16]),
    .Flag(alu_1_flag));
  and and_2 (and_2_out, counter_1_q, decoder_1_write_rreg);
  or or_1 (or_1_out, decoder_1_low_ram_addr_input__high_ram_addr_rreg, and_2_out);
  Register #(.width(16), .trigger("falling")) register_2 (
    .D(mux_16_5_output), .Q(register_2_q), .clk(decoder_1_j));  // open: en, clr
  Counter #(.width(1), .max('h1), .trigger("falling")) counter_1 (
    .D(alu_1_flag), .Q(counter_1_q), .clk(decoder_1_jmp_if_flag_or_j));  // open: load, count, carry, clr
  RAM #(.addrWidth(16), .dataWidth(16), .bus("separate")) ram_1 (
    .addr(register_2_q), .din(External_Out[15:0]), .data(ram_1_data), .clk(decoder_1_write_output),
    .clr(Reset));  // open: str, sel, ld
endmodule

module decoder (
  input  [3:0] in_1,
  input  Enable,
  output Low_RAM__High_INPUT,
  output Write_RA,
  output Write_RB,
  output Write_RAM,
  output Low_JMP_RAM__High_JMP_INPUT,
  output JMP_if_FLAG_or_J,
  output J,
  output Write_OUTPUT,
  output Read_INPUT,
  output Write_RREG,
  output Low_RAM_addr_INPUT__High_RAM_addr_RREG
);

  wire decoder_1_out1, decoder_1_out2, decoder_1_out3, decoder_1_out4, decoder_1_out5, decoder_1_out6,
       decoder_1_out7, decoder_1_out8, decoder_1_out9, decoder_1_out10, decoder_1_out11, decoder_1_out14,
       decoder_1_out15;

  Decoder #(.select(4), .disabled(0)) decoder_1 (
    .out1(decoder_1_out1), .out2(decoder_1_out2), .out3(decoder_1_out3), .out4(decoder_1_out4),
    .out5(decoder_1_out5), .out6(decoder_1_out6), .out7(decoder_1_out7), .out8(decoder_1_out8),
    .out9(decoder_1_out9), .out10(decoder_1_out10), .out11(decoder_1_out11), .out12(Read_INPUT),
    .out13(Write_RREG), .out14(decoder_1_out14), .out15(decoder_1_out15), .sel(in_1), .en(Enable));  // open: out0
  or or_1 (Low_RAM__High_INPUT, decoder_1_out1, decoder_1_out2, decoder_1_out10, Read_INPUT);
  or or_2 (Write_RA, decoder_1_out1, decoder_1_out3, Read_INPUT, decoder_1_out14);
  or or_3 (Write_RB, decoder_1_out2, decoder_1_out4, decoder_1_out15);
  or or_4 (Write_RAM, decoder_1_out5, Read_INPUT);
  or or_5 (Low_JMP_RAM__High_JMP_INPUT, decoder_1_out6, decoder_1_out8);
  or or_6 (JMP_if_FLAG_or_J, decoder_1_out6, decoder_1_out7, decoder_1_out8, decoder_1_out9);
  or or_7 (J, decoder_1_out8, decoder_1_out9);
  or or_8 (Write_OUTPUT, decoder_1_out10, decoder_1_out11);
  or or_9 (Low_RAM_addr_INPUT__High_RAM_addr_RREG, decoder_1_out11, decoder_1_out14, decoder_1_out15);
endmodule

module alu (
  input  [15:0] Input_A,
  input  [15:0] Input_B,
  input  [3:0] Operation,
  output Flag,
  output [15:0] Output
);

  wire comparator_1_eq, comparator_1_gt, comparator_1_lt, decoder_1_out0, decoder_1_out1, decoder_1_out2,
       decoder_1_out3, decoder_1_out4, decoder_1_out5, decoder_1_out6, decoder_1_out7, decoder_1_out8,
       decoder_1_out9, decoder_1_out10, decoder_1_out11, decoder_1_out12, decoder_1_out13, decoder_1_out14,
       decoder_1_out15, nor_1_out, nor_2_out, not_1_out;
  wire [15:0] adder_1_out, and_1_out, divider_1_out, divider_1_rem, multiplier_1_out, not_2_out, or_1_out,
       shifter_1_out, shifter_2_out, subtractor_1_out, xor_1_out;

  assign Output = decoder_1_out0 ? Input_A : 16'bz;  // Controlled_Buffer controlled_buffer_1
  Comparator #(.width(16)) comparator_1 (
    .a(Input_A), .b(Input_B), .gt(comparator_1_gt), .eq(comparator_1_eq), .lt(comparator_1_lt));
  not not_1 (not_1_out, comparator_1_eq);
  assign not_2_out = ~Input_A;  // NOT_Gate not_2, 16 bits wide
  assign Output = decoder_1_out5 ? not_2_out : 16'bz;  // Controlled_Buffer controlled_buffer_2
  assign Output = decoder_1_out6 ? adder_1_out : 16'bz;  // Controlled_Buffer controlled_buffer_3
  Adder #(.width(16)) adder_1 (.a(Input_A), .b(Input_B), .out(adder_1_out));  // open: cin, cout
  Subtractor #(.width(16)) subtractor_1 (.a(Input_A), .b(Input_B), .out(subtractor_1_out));  // open: bin, bout
  assign Output = decoder_1_out7 ? subtractor_1_out : 16'bz;  // Controlled_Buffer controlled_buffer_4
  Multiplier #(.width(16)) multiplier_1 (.a(Input_A), .b(Input_B), .out(multiplier_1_out));  // open: cin, cout
  assign Output = decoder_1_out8 ? multiplier_1_out : 16'bz;  // Controlled_Buffer controlled_buffer_5
  Divider #(.width(16)) divider_1 (.a(Input_A), .b(Input_B), .out(divider_1_out), .rem(divider_1_rem));  // open: upper
  assign Output = decoder_1_out9 ? divider_1_out : 16'bz;  // Controlled_Buffer controlled_buffer_6
  assign Output = decoder_1_out10 ? divider_1_rem : 16'bz;  // Controlled_Buffer controlled_buffer_7
  Shifter #(.width(16)) shifter_1 (.in(Input_A), .\dist (Input_B[3:0]), .out(shifter_1_out));
  assign Output = decoder_1_out11 ? shifter_1_out : 16'bz;  // Controlled_Buffer controlled_buffer_8
  Shifter #(.width(16), .shift("lr")) shifter_2 (.in(Input_A), .\dist (Input_B[3:0]), .out(shifter_2_out));
  assign Output = decoder_1_out12 ? shifter_2_out : 16'bz;  // Controlled_Buffer controlled_buffer_9
  assign xor_1_out = Input_A ^ Input_B;  // XOR_Gate xor_1, 16 bits wide
  assign Output = decoder_1_out13 ? xor_1_out : 16'bz;  // Controlled_Buffer controlled_buffer_10
  assign Output = decoder_1_out14 ? and_1_out : 16'bz;  // Controlled_Buffer controlled_buffer_11
  assign and_1_out = Input_A & Input_B;  // AND_Gate and_1, 16 bits wide
  assign or_1_out = Input_A | Input_B;  // OR_Gate or_1, 16 bits wide
  assign Output = decoder_1_out15 ? or_1_out : 16'bz;  // Controlled_Buffer controlled_buffer_12
  assign Flag = nor_1_out ? 1'b0 : 1'bz;  // Controlled_Buffer controlled_buffer_13
  nor nor_1 (nor_1_out, decoder_1_out1, decoder_1_out2, decoder_1_out3, decoder_1_out4);
  assign Flag = decoder_1_out1 ? comparator_1_gt : 1'bz;  // Controlled_Buffer controlled_buffer_14
  assign Flag = decoder_1_out2 ? comparator_1_eq : 1'bz;  // Controlled_Buffer controlled_buffer_15
  assign Flag = decoder_1_out3 ? comparator_1_lt : 1'bz;  // Controlled_Buffer controlled_buffer_16
  assign Flag = decoder_1_out4 ? not_1_out : 1'bz;  // Controlled_Buffer controlled_buffer_17
  assign Output = nor_2_out ? {16{1'b0}} : 16'bz;  // Controlled_Buffer controlled_buffer_18
  nor nor_2 (nor_2_out, decoder_1_out5, decoder_1_out6, decoder_1_out7, decoder_1_out8, decoder_1_out9, decoder_1_out10, decoder_1_out12, decoder_1_out13, decoder_1_out14, decoder_1_out15, decoder_1_out0);
  Decoder #(.select(4)) decoder_1 (
    .out0(decoder_1_out0), .out1(decoder_1_out1), .out2(decoder_1_out2), .out3(decoder_1_out3),
    .out4(decoder_1_out4), .out5(decoder_1_out5), .out6(decoder_1_out6), .out7(decoder_1_out7),
    .out8(decoder_1_out8), .out9(decoder_1_out9), .out10(decoder_1_out10), .out11(decoder_1_out11),
    .out12(decoder_1_out12), .out13(decoder_1_out13), .out14(decoder_1_out14), .out15(decoder_1_out15),
    .sel(Operation));  // open: en
endmodule

module mux_16 (
  input  [15:0] Input_A,
  input  [15:0] Input_B,
  input  Select,
  output [15:0] Output
);

  wire not_1_out;

  not not_1 (not_1_out, Select);
  assign Output = not_1_out ? Input_A : 16'bz;  // Controlled_Buffer controlled_buffer_1
  assign Output = Select ? Input_B : 16'bz;  // Controlled_Buffer controlled_buffer_2
endmodule

module extern_out (
  input  [16:0] Input,
  output [15:0] Output,
  output Clock
);

  Register #(.width(16)) register_1 (.D(Input[15:0]), .Q(Output), .clk(Input[16]));  // open: en, clr

  assign Clock = Input[16];
endmodule
